# Fritzing sketch sensor (saved by Fritzing 0.9.3b)
breadboards: 1

parts:
  Q1 = TRANSISTOR_NPN [package=to-92-ammo]
  R1 = Resistor [tolerance=±5% resistance=1k package="1206 [SMD]"]
  LED1 = smd LED [color="Red (633nm)" package="0805 [SMD]"]
  R2 = Resistor [tolerance=±5% resistance=220 package="1206 [SMD]"]
  S1 = Toggle Switch [package=THT]
  R3 = Resistor [tolerance=±5% resistance=1M package=THT]

nets:
  N1: Q1.E, R2.Pin_0
  N2: Q1.B, R1.Pin_1, R3.Pin_0
  N3: Q1.C, R3.Pin_1
  N4: R1.Pin_0, S1.COM
  N5: LED1.cathode, R2.Pin_1
  N6: LED1.anode, S1.L2

notes:
  B
  A
  5 Vin
  Vout (3.7)
  GND
